# Fritzing sketch L293B-with-two-motors-version2 (saved by Fritzing 0.7.11b)
breadboards: 1

parts:
  D1 = Rectifier Diode [part_number=1N4001 package="300 mil [THT]"]
  D2 = Rectifier Diode [part_number=1N4001 package="300 mil [THT]"]
  D3 = Rectifier Diode [part_number=1N4001 package="300 mil [THT]"]
  D4 = Rectifier Diode [part_number=1N4001 package="300 mil [THT]"]
  IC1 = L293D [package=THT]
  M1 = DC Motor
  D5 = Rectifier Diode [part_number=1N4001 package="300 mil [THT]"]
  D6 = Rectifier Diode [part_number=1N4001 package="300 mil [THT]"]
  D7 = Rectifier Diode [part_number=1N4001 package="300 mil [THT]"]
  D8 = Rectifier Diode [part_number=1N4001 package="300 mil [THT]"]
  M2 = DC Motor
  VCC1 = Battery block 9V
  Arduino1 = Arduino

nets:
  N1: D1.cathode, D2.cathode, D5.cathode, D6.cathode, VCC1.+
  N2: D1.anode, D3.cathode, IC1.Out_1_(_Controlled_by_Enable_1_), M1.pin_1
  N3: D2.anode, D4.cathode, IC1.Out_2_(_Controlled_by_Enable_1_), M1.pin_2
  N4: D3.anode, D4.anode, IC1.0V, D7.anode, D8.anode, VCC1.-, Arduino1.GND
  N5: IC1.Out_3_(_Controlled_by_Enable_2_), D5.anode, D8.cathode, M2.pin_2
  N6: IC1.Out_4_(_Controlled_by_Enable_2_), D6.anode, D7.cathode, M2.pin_1
  N7: IC1.+V, Arduino1.+5V
