# Fritzing sketch L293B-with-two-motors-version3 (saved by Fritzing 0.7.11b)
breadboards: 1

parts:
  D1 = Rectifier Diode [part_number=1N4001 package="300 mil [THT]"]
  D2 = Rectifier Diode [part_number=1N4001 package="300 mil [THT]"]
  D3 = Rectifier Diode [part_number=1N4001 package="300 mil [THT]"]
  D4 = Rectifier Diode [part_number=1N4001 package="300 mil [THT]"]
  M1 = DC Motor
  IC1 = L293D [package=THT]
  VCC1 = Battery block 9V
  D5 = Rectifier Diode [part_number=1N4001 package="300 mil [THT]"]
  D6 = Rectifier Diode [part_number=1N4001 package="300 mil [THT]"]
  D7 = Rectifier Diode [part_number=1N4001 package="300 mil [THT]"]
  D8 = Rectifier Diode [part_number=1N4001 package="300 mil [THT]"]
  M2 = DC Motor
  Arduino1 = Arduino
  R1 = Resistor [tolerance=±5% resistance=220 package=THT]
  R2 = Resistor [tolerance=±5% resistance=220 package=THT]

nets (from the breadboard view):
  N1: D1.cathode, D2.cathode, IC1.+Vmotor, VCC1.+, D7.cathode, D8.cathode
  N2: D1.anode, D3.cathode, M1.pin_1, IC1.Out_2_(_Controlled_by_Enable_1_)
  N3: D2.anode, D4.cathode, M1.pin_2, IC1.Out_1_(_Controlled_by_Enable_1_)
  N4: D3.anode, D4.anode, IC1.0V, VCC1.-, D5.anode, D6.anode, Arduino1.GND, R1.Pin_1, R2.Pin_0
  N5: IC1.Enable_1, Arduino1.D2, R1.Pin_0
  N6: IC1.In_1, Arduino1.D3
  N7: IC1.In_2, Arduino1.D4
  N8: IC1.Enable_2, Arduino1.D5, R2.Pin_1
  N9: IC1.In_3, Arduino1.D6
  N10: IC1.Out_3_(_Controlled_by_Enable_2_), D5.cathode, D7.anode, M2.pin_1
  N11: IC1.Out_4_(_Controlled_by_Enable_2_), D6.cathode, D8.anode, M2.pin_2
  N12: IC1.In_4, Arduino1.D7
  N13: IC1.+V, Arduino1.+5V
