# Fritzing sketch L293B-with-two-motors (saved by Fritzing 0.7.11b)
breadboards: 1

parts:
  IC1 = L293D [package=THT]
  D1 = Rectifier Diode [part_number=1N4001 package="300 mil [THT]"]
  D2 = Rectifier Diode [part_number=1N4001 package="300 mil [THT]"]
  D3 = Rectifier Diode [part_number=1N4001 package="300 mil [THT]"]
  D4 = Rectifier Diode [part_number=1N4001 package="300 mil [THT]"]
  M1 = DC Motor
  D5 = Rectifier Diode [part_number=1N4001 package="300 mil [THT]"]
  D6 = Rectifier Diode [part_number=1N4001 package="300 mil [THT]"]
  D7 = Rectifier Diode [part_number=1N4001 package="300 mil [THT]"]
  D8 = Rectifier Diode [part_number=1N4001 package="300 mil [THT]"]
  M2 = DC Motor

nets:
  N1: IC1.Out_1_(_Controlled_by_Enable_1_), D1.cathode, D3.anode, M1.pin_2
  GND: IC1.0V, D1.anode, D2.anode, D5.anode, D6.anode
  N2: IC1.Out_2_(_Controlled_by_Enable_1_), D2.cathode, D4.anode, M1.pin_1
  N3: IC1.+Vmotor, D3.cathode, D4.cathode, D7.cathode, D8.cathode
  N4: IC1.Out_3_(_Controlled_by_Enable_2_), D5.cathode, D7.anode, M2.pin_2
  N5: IC1.Out_4_(_Controlled_by_Enable_2_), D6.cathode, D8.anode, M2.pin_1
